# Fritzing sketch MarqueeN (saved by Fritzing 0.9.3b)
circuit board: 6.66478cm x 6.50001cm
breadboards: 1

parts:
  LED1 = LED - 5mm [color="Red (633nm)" package="5 mm [THT]"]
  LED2 = LED - 5mm [color="Red (633nm)" package="5 mm [THT]"]
  LED3 = LED - 5mm [color="Red (633nm)" package="5 mm [THT]"]
  LED4 = LED - 5mm [color="Red (633nm)" package="5 mm [THT]"]
  LED6 = LED - 5mm [color="Red (633nm)" package="5 mm [THT]"]
  LED7 = LED - 5mm [color="Red (633nm)" package="5 mm [THT]"]
  LED8 = LED - 5mm [color="Red (633nm)" package="5 mm [THT]"]
  LED9 = LED - 5mm [color="Red (633nm)" package="5 mm [THT]"]
  LED10 = LED - 5mm [color="Red (633nm)" package="5 mm [THT]"]
  LED11 = LED - 5mm [color="Red (633nm)" package="5 mm [THT]"]
  LED12 = LED - 5mm [color="Red (633nm)" package="5 mm [THT]"]
  LED5 = LED - 5mm [color="Red (633nm)" package="5 mm [THT]"]
  R1 = Resistor [tolerance=±5% resistance=33 package=THT]
  R2 = Resistor [tolerance=±5% resistance=33 package=THT]
  R3 = Resistor [tolerance=±5% resistance=33 package=THT]
  R4 = Resistor [tolerance=±5% resistance=33 package=THT]
  R5 = Resistor [tolerance=±5% resistance=33 package=THT]
  R6 = Resistor [tolerance=±5% resistance=33 package=THT]
  J2 = female pin header, 2 pins [form="♀ (female)"]
  J1 = female pin header, 2 pins [form="♀ (female)"]

nets:
  N1: LED1.cathode, LED2.anode
  5V: LED1.anode, LED3.anode, LED7.anode, LED9.anode, LED11.anode, LED5.anode, J2.pin1, J1.pin1
  N2: LED2.cathode, R1.Pin_0
  N3: LED3.cathode, LED4.anode
  N4: LED4.cathode, R2.Pin_0
  N5: LED6.cathode, R3.Pin_0
  N6: LED6.anode, LED5.cathode
  N7: LED7.cathode, LED8.anode
  N8: LED8.cathode, R4.Pin_0
  N9: LED9.cathode, LED10.anode
  N10: LED10.cathode, R5.Pin_0
  N11: LED11.cathode, LED12.anode
  N12: LED12.cathode, R6.Pin_0
  N13: R1.Pin_1, R2.Pin_1, R3.Pin_1
  N14: R4.Pin_1, R5.Pin_1
  GND: R6.Pin_1, J2.pin2, J1.pin2
