# Fritzing sketch PCB-B-small-GP (saved by Fritzing 0.9.3b)
circuit board: 4.42374cm x 4.99999cm
breadboards: 1

parts:
  R7 = Resistor [tolerance=±5% resistance=33 package=THT]
  R8 = Resistor [tolerance=±5% resistance=33 package=THT]
  R9 = Resistor [tolerance=±5% resistance=33 package=THT]
  R10 = Resistor [tolerance=±5% resistance=33 package=THT]
  R11 = Resistor [tolerance=±5% resistance=33 package=THT]
  R12 = Resistor [tolerance=±5% resistance=33 package=THT]
  J3 = female pin header, 2 pins [form="♀ (female)"]
  J4 = female pin header, 2 pins [form="♀ (female)"]
  LED16 = LED - 3mm [color="Red (633nm)" package="3 mm [THT]"]
  LED15 = LED - 3mm [color="Red (633nm)" package="3 mm [THT]"]
  LED20 = LED - 3mm [color="Red (633nm)" package="3 mm [THT]"]
  LED13 = LED - 3mm [color="Red (633nm)" package="3 mm [THT]"]
  LED21 = LED - 3mm [color="Red (633nm)" package="3 mm [THT]"]
  LED22 = LED - 3mm [color="Red (633nm)" package="3 mm [THT]"]
  LED14 = LED - 3mm [color="Red (633nm)" package="3 mm [THT]"]
  LED23 = LED - 3mm [color="Red (633nm)" package="3 mm [THT]"]
  LED17 = LED - 3mm [color="Red (633nm)" package="3 mm [THT]"]
  LED18 = LED - 3mm [color="Red (633nm)" package="3 mm [THT]"]
  LED19 = LED - 3mm [color="Red (633nm)" package="3 mm [THT]"]
  LED24 = LED - 3mm [color="Red (633nm)" package="3 mm [THT]"]

nets:
  N1: R7.Pin_0, LED14.cathode
  GND: R7.Pin_1, J3.pin2, J4.pin2
  N2: R8.Pin_0, LED16.cathode
  N3: R8.Pin_1, R9.Pin_1
  N4: R9.Pin_0, LED18.cathode
  N5: R10.Pin_0, LED20.cathode
  N6: R10.Pin_1, R11.Pin_1, R12.Pin_1
  N7: R11.Pin_0, LED21.cathode
  N8: R12.Pin_0, LED23.cathode
  5V: J3.pin1, J4.pin1, LED15.anode, LED13.anode, LED22.anode, LED17.anode, LED19.anode, LED24.anode
  N9: LED16.anode, LED17.cathode
  N10: LED15.cathode, LED14.anode
  N11: LED20.anode, LED13.cathode
  N12: LED21.anode, LED22.cathode
  N13: LED23.anode, LED24.cathode
  N14: LED18.anode, LED19.cathode

notes:
  -
