# Fritzing sketch PCB-B-small-batt (saved by Fritzing 0.9.3b)
circuit board: 4.42374cm x 4.99999cm
breadboards: 1

parts:
  LED16 = LED - 3mm [color="Red (633nm)" package="3 mm [THT]"]
  LED15 = LED - 3mm [color="Red (633nm)" package="3 mm [THT]"]
  LED20 = LED - 3mm [color="Red (633nm)" package="3 mm [THT]"]
  LED13 = LED - 3mm [color="Red (633nm)" package="3 mm [THT]"]
  LED21 = LED - 3mm [color="Red (633nm)" package="3 mm [THT]"]
  LED22 = LED - 3mm [color="Red (633nm)" package="3 mm [THT]"]
  LED14 = LED - 3mm [color="Red (633nm)" package="3 mm [THT]"]
  LED23 = LED - 3mm [color="Red (633nm)" package="3 mm [THT]"]
  LED17 = LED - 3mm [color="Red (633nm)" package="3 mm [THT]"]
  LED18 = LED - 3mm [color="Red (633nm)" package="3 mm [THT]"]
  LED19 = LED - 3mm [color="Red (633nm)" package="3 mm [THT]"]
  BAT1 = Battery Holders [package=battcon_12mm]
  S1 = SPST Switch [package=ayz0202]
  LED24 = LED - 3mm [color="Red (633nm)" package="3 mm [THT]"]
  R1 = Resistor [tolerance=±5% resistance=220 package=THT]

nets:
  GND: LED16.cathode, LED15.cathode, LED20.cathode, LED13.cathode, LED21.cathode, LED22.cathode, LED14.cathode, LED23.cathode, LED17.cathode, LED18.cathode, LED19.cathode, S1.P, LED24.cathode
  5V: LED16.anode, LED15.anode, LED20.anode, LED13.anode, LED21.anode, LED22.anode, LED14.anode, LED23.anode, LED17.anode, LED18.anode, LED19.anode, BAT1.+, LED24.anode
  N1: BAT1.-, R1.Pin_0
  N2: S1.O, R1.Pin_1
