# Fritzing sketch PCB-B-small (saved by Fritzing 0.9.3b)
circuit board: 8.84748cm x 10cm
breadboards: 1

parts:
  LED13 = LED - 5mm [color="Red (633nm)" package="5 mm [THT]"]
  LED14 = LED - 5mm [color="Red (633nm)" package="5 mm [THT]"]
  LED15 = LED - 5mm [color="Red (633nm)" package="5 mm [THT]"]
  LED16 = LED - 5mm [color="Red (633nm)" package="5 mm [THT]"]
  LED17 = LED - 5mm [color="Red (633nm)" package="5 mm [THT]"]
  LED18 = LED - 5mm [color="Red (633nm)" package="5 mm [THT]"]
  LED19 = LED - 5mm [color="Red (633nm)" package="5 mm [THT]"]
  LED20 = LED - 5mm [color="Red (633nm)" package="5 mm [THT]"]
  LED21 = LED - 5mm [color="Red (633nm)" package="5 mm [THT]"]
  LED22 = LED - 5mm [color="Red (633nm)" package="5 mm [THT]"]
  LED23 = LED - 5mm [color="Red (633nm)" package="5 mm [THT]"]
  LED24 = LED - 5mm [color="Red (633nm)" package="5 mm [THT]"]
  R7 = Resistor [tolerance=±5% resistance=33 package=THT]
  R8 = Resistor [tolerance=±5% resistance=33 package=THT]
  R9 = Resistor [tolerance=±5% resistance=33 package=THT]
  R10 = Resistor [tolerance=±5% resistance=33 package=THT]
  R11 = Resistor [tolerance=±5% resistance=33 package=THT]
  R12 = Resistor [tolerance=±5% resistance=33 package=THT]
  J3 = female pin header, 2 pins [form="♀ (female)"]
  J4 = female pin header, 2 pins [form="♀ (female)"]

nets:
  N1: LED13.cathode, LED20.anode
  5V: LED13.anode, LED15.anode, LED17.anode, LED19.anode, LED22.anode, LED24.anode, J3.pin1, J4.pin1
  N2: LED14.cathode, R7.Pin_0
  N3: LED14.anode, LED15.cathode
  N4: LED16.cathode, R8.Pin_0
  N5: LED16.anode, LED17.cathode
  N6: LED18.cathode, R9.Pin_0
  N7: LED18.anode, LED19.cathode
  N8: LED20.cathode, R10.Pin_0
  N9: LED21.cathode, R11.Pin_0
  N10: LED21.anode, LED22.cathode
  N11: LED23.cathode, R12.Pin_0
  N12: LED23.anode, LED24.cathode
  GND: R7.Pin_1, J3.pin2, J4.pin2
  N13: R8.Pin_1, R9.Pin_1
  N14: R10.Pin_1, R11.Pin_1, R12.Pin_1

notes:
  -
